# Fritzing sketch CouvertureChauffanteSchema (saved by Fritzing 0.8.7b)
breadboards: 1

parts:
  Composant1 = Arduino Uno (Rev3)
  LCD1 = LCD screen
  S1 = Pushbutton [package="[THT]"]
  S2 = Pushbutton [package="[THT]"]
  S3 = Pushbutton [package="[THT]"]
  S4 = Pushbutton [package="[THT]"]
  R1 = Resistor [tolerance=±5% resistance=220 package=THT]

nets:
  N1: Composant1.D11_PWM/MOSI, LCD1.E
  N2: Composant1.D12/MISO, LCD1.RS
  N3: Composant1.D2, LCD1.DB7
  N4: Composant1.D3_PWM, LCD1.DB6
  N5: Composant1.D4, LCD1.DB5
  N6: Composant1.D5_PWM, LCD1.DB4
  N7: Composant1.D6_PWM, LCD1.V0
  5V: Composant1.5V, LCD1.VDD, R1.Pin_1
  GND: Composant1.GND, LCD1.VSS, LCD1.R/W, LCD1.LED-, S1.Pin_3, S1.Pin_4, S2.Pin_3, S2.Pin_4, S3.Pin_3, S3.Pin_4, S4.Pin_3, S4.Pin_4
  N8: LCD1.LED+, R1.Pin_0
  N9: S1.Pin_1, S1.Pin_2
  N10: S2.Pin_1, S2.Pin_2
  N11: S3.Pin_1, S3.Pin_2
  N12: S4.Pin_1, S4.Pin_2
